// Logisim project 4bit_t1.circ as structural Verilog: 6 circuits, main circuit main
module main (
  input  clear_ALL,
  output [3:0] out_2
);

  wire clock_1_out, controlled_buffer_4_out, controlunitv1_1_chlt, mycomparater_1_equalzero, not_1_out;
  wire [2:0] undriven;
  wire [3:0] ACC_q, alu_4bit_1_cpu_out, controlled_buffer_1_out, controlled_buffer_5_out,
       controlled_buffer_6_out, controlunitv1_1_cycle_out, InstructionRegister_q, OutputRegister_q,
       ram_1_dout, RegisterA_q, undriven_2;
  wire [7:0] controlled_buffer_2_out, controlled_buffer_3_out, counter_1_q, MemoryAddressRegister_q;
  wire [20:0] controlunitv1_1_controlbits;

  assign controlled_buffer_1_out = controlunitv1_1_controlbits[11] ? controlled_buffer_5_out : 4'bz;  // Controlled_Buffer controlled_buffer_1
  Counter counter_1 (
    .load(controlunitv1_1_controlbits[19]), .D(controlled_buffer_2_out),
    .count(controlunitv1_1_controlbits[18]), .Q(counter_1_q), .clk(controlled_buffer_4_out),
    .clr(controlunitv1_1_controlbits[17]));  // open: carry, up
  Register MemoryAddressRegister (
    .D(controlled_buffer_3_out), .en(controlunitv1_1_controlbits[15]), .clk(controlled_buffer_4_out),
    .Q(MemoryAddressRegister_q), .clr(controlunitv1_1_controlbits[14]));
  RAM #(.asyncread("true"), .dataWidth(4), .\type ("nonvolatile")) ram_1 (
    .addr(MemoryAddressRegister_q), .we(controlunitv1_1_controlbits[13]),
    .oe(controlunitv1_1_controlbits[12]), .clk(controlled_buffer_4_out), .din(controlled_buffer_1_out),
    .dout(ram_1_dout));
  Register #(.width(4)) InstructionRegister (
    .D(controlled_buffer_5_out), .en(controlunitv1_1_controlbits[9]), .clk(controlled_buffer_4_out),
    .Q(InstructionRegister_q), .clr(controlunitv1_1_controlbits[8]));
  assign controlled_buffer_2_out = controlunitv1_1_controlbits[20] ? controlled_buffer_3_out : 8'bz;  // Controlled_Buffer controlled_buffer_2
  assign controlled_buffer_3_out = controlunitv1_1_controlbits[16] ? counter_1_q : 8'bz;  // Controlled_Buffer controlled_buffer_3
  assign controlled_buffer_4_out = not_1_out ? clock_1_out : 1'bz;  // Controlled_Buffer controlled_buffer_4
  Clock clock_1 (.out(clock_1_out));
  not not_1 (not_1_out, controlunitv1_1_chlt);
  controlUnitV1 controlunitv1_1 (
    .CLK(controlled_buffer_4_out), .instruction(InstructionRegister_q), .clear_ALL(clear_ALL),
    .cHLT(controlunitv1_1_chlt), .cycle_out(controlunitv1_1_cycle_out), .cmdregOUT(out_2),
    .controlBits(controlunitv1_1_controlbits));  // open: address
  assign controlled_buffer_5_out = controlunitv1_1_controlbits[10] ? ram_1_dout : 4'bz;  // Controlled_Buffer controlled_buffer_5
  Hex_Digit_Display hex_digit_display_1 (.value(controlunitv1_1_cycle_out));  // open: dp
  Register #(.width(4)) OutputRegister (
    .D(undriven_2), .en(controlunitv1_1_controlbits[7]), .clk(controlled_buffer_4_out), .Q(OutputRegister_q),
    .clr(controlunitv1_1_controlbits[6]));
  Register #(.width(4)) ACC (
    .D(controlled_buffer_6_out), .en(controlunitv1_1_controlbits[1]), .clk(controlled_buffer_4_out),
    .Q(ACC_q), .clr(controlunitv1_1_controlbits[0]));
  assign controlled_buffer_6_out = controlunitv1_1_controlbits[2] ? ACC_q : 4'bz;  // Controlled_Buffer controlled_buffer_6
  Register #(.width(4)) RegisterA (
    .D(controlled_buffer_6_out), .en(controlunitv1_1_controlbits[5]), .clk(controlled_buffer_4_out),
    .Q(RegisterA_q), .clr(controlunitv1_1_controlbits[4]));
  Hex_Digit_Display hex_digit_display_2 (.value(OutputRegister_q));  // open: dp
  assign controlled_buffer_6_out = controlunitv1_1_controlbits[3] ? alu_4bit_1_cpu_out : 4'bz;  // Controlled_Buffer controlled_buffer_7
  myComparater mycomparater_1 (.in_1(ACC_q), .equalZero(mycomparater_1_equalzero));
  ALU_4bit alu_4bit_1 (.a(ACC_q), .b(RegisterA_q), .opcode(undriven), .cpu_out(alu_4bit_1_cpu_out));
  LED led_1 (.in(mycomparater_1_equalzero));

  // Notes on the sheet:
  //   PC-MAR-RAM-IR
endmodule

module ALU_4bit (
  input  [3:0] a,
  input  [3:0] b,
  input  [2:0] opcode,
  output [3:0] cpu_out
);

  wire [3:0] adder_1_out, and_1_out, not_1_out, or_1_out, subtractor_1_out, xor_1_out;

  Adder #(.width(4)) adder_1 (.a(a), .b(b), .out(adder_1_out));  // open: cin, cout
  Subtractor #(.width(4)) subtractor_1 (.a(a), .b(b), .out(subtractor_1_out));  // open: bin, bout
  assign and_1_out = a & b;  // AND_Gate and_1, 4 bits wide
  assign or_1_out = a | b;  // OR_Gate or_1, 4 bits wide
  assign not_1_out = ~a;  // NOT_Gate not_1, 4 bits wide
  assign xor_1_out = a ^ b;  // XOR_Gate xor_1, 4 bits wide
  Multiplexer #(.select(3), .width(4)) multiplexer_1 (
    .in0(adder_1_out), .in1(subtractor_1_out), .in2(and_1_out), .in3(or_1_out), .in4(xor_1_out),
    .in5(not_1_out), .out(cpu_out), .sel(opcode));  // open: in6, in7
endmodule

module controlUnitV1 (
  input  CLK,
  input  [3:0] instruction,
  input  clear_ALL,
  output cHLT,
  output [3:0] cycle_out,
  output [3:0] cmdregOUT,
  output [20:0] controlBits,
  output [7:0] address
);

  wire ADD, and_1_out, cAND, cNOT, cOR, cOUT, cXOR, decoder_2_out0, decoder_2_out1, decoder_2_out2,
       decoder_2_out3, decoder_2_out4, decoder_2_out5, decoder_2_out6, decoder_2_out7, decoder_2_out8, HLT,
       INC, JE, JGT, JLT, JMP, JNE, LDA, left_bit_we, right_bit_we, STA, SUB, t3_l_out, undriven, undriven_2;
  wire [3:0] demultiplexer_1_out0, demultiplexer_1_out1, left_bit_q, right_bit_q;

  Register #(.width(4)) command (.D(instruction), .en(decoder_2_out2), .clk(and_1_out), .Q(cmdregOUT), .clr(clear_ALL));
  Demultiplexer #(.width(4)) demultiplexer_1 (
    .out0(demultiplexer_1_out0), .out1(demultiplexer_1_out1), .in(instruction), .sel(undriven));
  Decoder #(.enable("false"), .select(4)) decoder_1 (
    .out0(HLT), .out1(LDA), .out2(STA), .out3(ADD), .out4(SUB), .out5(cAND), .out6(cOR), .out7(cXOR),
    .out8(cNOT), .out9(INC), .out10(cOUT), .out11(JMP), .out12(JNE), .out13(JE), .out14(JLT), .out15(JGT),
    .sel(cmdregOUT));
  Register #(.width(4)) right_bit (
    .D(demultiplexer_1_out0), .en(left_bit_we), .clk(CLK), .Q(right_bit_q), .clr(clear_ALL));
  Register #(.width(4)) left_bit (
    .D(demultiplexer_1_out1), .en(right_bit_we), .clk(CLK), .Q(left_bit_q), .clr(clear_ALL));
  buf pc_input_get_dataline (controlBits[20], 1'b0);  // OR_Gate
  buf pc_loadData_enable (controlBits[19], 1'b0);  // OR_Gate
  or pc_enable (controlBits[18], decoder_2_out0, t3_l_out);
  or pc_output_to_addressline (controlBits[16], decoder_2_out0, t3_l_out);
  or mar_we (controlBits[15], decoder_2_out0, t3_l_out);
  buf ram_write_enable (controlBits[13], 1'b0);  // OR_Gate
  buf ram_output_enable (controlBits[12], decoder_2_out1);  // OR_Gate
  buf ram_input_in_dataline (controlBits[11], 1'b0);  // OR_Gate
  buf ram_output_to_dataline (controlBits[10], decoder_2_out1);  // OR_Gate
  buf ins_we (controlBits[9], decoder_2_out1);  // OR_Gate
  buf regOUT_we (controlBits[7], 1'b0);  // OR_Gate
  buf rega_we (controlBits[5], 1'b0);  // OR_Gate
  buf cpu_output_to_dataline (controlBits[3], 1'b0);  // OR_Gate
  buf acc_output_to_dataLine (controlBits[2], 1'b0);  // OR_Gate
  buf ACC_WE (controlBits[1], 1'b0);  // OR_Gate
  assign address = undriven_2 ? {left_bit_q, right_bit_q} : 8'bz;  // Controlled_Buffer controlled_buffer_1
  and and_1 (and_1_out, ~cHLT, CLK);  // AND_Gate
  Counter #(.max('hf), .width(4)) counter_1 (
    .count(and_1_out), .Q(cycle_out), .clk(and_1_out), .clr(decoder_2_out8));  // open: load, D, carry, up
  Decoder #(.enable("false"), .select(4)) decoder_2 (
    .out0(decoder_2_out0), .out1(decoder_2_out1), .out2(decoder_2_out2), .out3(decoder_2_out3),
    .out4(decoder_2_out4), .out5(decoder_2_out5), .out6(decoder_2_out6), .out7(decoder_2_out7),
    .out8(decoder_2_out8), .sel(cycle_out));  // open: out9, out10, out11, out12, out13, out14, out15
  and and_2 (cHLT, decoder_2_out3, HLT);
  and t3_l (t3_l_out, decoder_2_out3, LDA);

  assign {controlBits[17], controlBits[14], controlBits[8], controlBits[6], controlBits[4], controlBits[0]} = {6{clear_ALL}};

  // Other names for the same wires on the sheet: address_t[3:0] = instruction

  // Notes on the sheet:
  //   INSTRUCTION DECODER
  //   CONTROL BITS
  //   RING COUNTER
endmodule

module myComparater (
  input  [3:0] in_1,
  output equalZero
);

  wire and_1_out, and_2_out, and_3_out, and_4_out, and_5_out, and_6_out;

  and and_1 (and_1_out, ~1'b0, ~in_1[0]);  // AND_Gate
  and and_2 (and_2_out, ~1'b0, ~in_1[1]);  // AND_Gate
  and and_3 (and_3_out, ~1'b0, ~in_1[2]);  // AND_Gate
  and and_4 (and_4_out, ~1'b0, ~in_1[3]);  // AND_Gate
  and and_5 (and_5_out, and_1_out, and_2_out);
  and and_6 (and_6_out, and_3_out, and_4_out);
  and and_7 (equalZero, and_5_out, and_6_out);
endmodule

module CPU_4bit (
  input  [3:0] ramInput,
  input  CLK,
  input  clear_CPU,
  output [3:0] regACC,
  output [7:0] PC,
  output [7:0] ramAddress,
  output ramWE,
  output [3:0] regA,
  output ramOutEnb,
  output [3:0] ramOutput,
  output [3:0] insReg,
  output [3:0] regOut,
  output [3:0] cmdRegOUT
);

  wire controlled_buffer_4_out, controlunitv1_1_chlt, mycomparater_1_equalzero, not_1_out;
  wire [2:0] undriven;
  wire [3:0] alu_4bit_1_cpu_out, controlled_buffer_5_out, controlled_buffer_6_out, controlunitv1_1_cycle_out,
       undriven_2;
  wire [7:0] controlled_buffer_2_out, controlled_buffer_3_out;
  wire [20:0] controlunitv1_1_controlbits;

  assign ramOutput = controlunitv1_1_controlbits[11] ? controlled_buffer_5_out : 4'bz;  // Controlled_Buffer controlled_buffer_1
  Counter counter_1 (
    .load(controlunitv1_1_controlbits[19]), .D(controlled_buffer_2_out),
    .count(controlunitv1_1_controlbits[18]), .Q(PC), .clk(controlled_buffer_4_out),
    .clr(controlunitv1_1_controlbits[17]));  // open: carry, up
  Register MemoryAddressRegister (
    .D(controlled_buffer_3_out), .en(controlunitv1_1_controlbits[15]), .clk(controlled_buffer_4_out),
    .Q(ramAddress), .clr(controlunitv1_1_controlbits[14]));
  Register #(.width(4)) InstructionRegister (
    .D(controlled_buffer_5_out), .en(controlunitv1_1_controlbits[9]), .clk(controlled_buffer_4_out),
    .Q(insReg), .clr(controlunitv1_1_controlbits[8]));
  assign controlled_buffer_2_out = controlunitv1_1_controlbits[20] ? controlled_buffer_3_out : 8'bz;  // Controlled_Buffer controlled_buffer_2
  assign controlled_buffer_3_out = controlunitv1_1_controlbits[16] ? PC : 8'bz;  // Controlled_Buffer controlled_buffer_3
  assign controlled_buffer_4_out = not_1_out ? CLK : 1'bz;  // Controlled_Buffer controlled_buffer_4
  not not_1 (not_1_out, controlunitv1_1_chlt);
  controlUnitV1 controlunitv1_1 (
    .CLK(controlled_buffer_4_out), .instruction(insReg), .clear_ALL(clear_CPU), .cHLT(controlunitv1_1_chlt),
    .cycle_out(controlunitv1_1_cycle_out), .cmdregOUT(cmdRegOUT),
    .controlBits({controlunitv1_1_controlbits[20:14], ramWE, ramOutEnb, controlunitv1_1_controlbits[11:0]}),
    .address(controlunitv1_1_controlbits[7:0]));
  assign controlled_buffer_5_out = controlunitv1_1_controlbits[10] ? ramInput : 4'bz;  // Controlled_Buffer controlled_buffer_5
  Hex_Digit_Display hex_digit_display_1 (.value(controlunitv1_1_cycle_out));  // open: dp
  Register #(.width(4)) OutputRegister (
    .D(undriven_2), .en(controlunitv1_1_controlbits[7]), .clk(controlled_buffer_4_out), .Q(regOut),
    .clr(controlunitv1_1_controlbits[6]));
  Register #(.width(4)) ACC (
    .D(controlled_buffer_6_out), .en(controlunitv1_1_controlbits[1]), .clk(controlled_buffer_4_out),
    .Q(regACC), .clr(controlunitv1_1_controlbits[0]));
  assign controlled_buffer_6_out = controlunitv1_1_controlbits[2] ? regACC : 4'bz;  // Controlled_Buffer controlled_buffer_6
  Register #(.width(4)) RegisterA (
    .D(controlled_buffer_6_out), .en(controlunitv1_1_controlbits[5]), .clk(controlled_buffer_4_out),
    .Q(regA), .clr(controlunitv1_1_controlbits[4]));
  Hex_Digit_Display hex_digit_display_2 (.value(regOut));  // open: dp
  assign controlled_buffer_6_out = controlunitv1_1_controlbits[3] ? alu_4bit_1_cpu_out : 4'bz;  // Controlled_Buffer controlled_buffer_7
  myComparater mycomparater_1 (.in_1(regACC), .equalZero(mycomparater_1_equalzero));
  ALU_4bit alu_4bit_1 (.a(regACC), .b(regA), .opcode(undriven), .cpu_out(alu_4bit_1_cpu_out));
  LED led_1 (.in(mycomparater_1_equalzero));
  // Pins of 8 and 21 bits meet at {controlunitv1_1_controlbits[20:14], ramWE, ramOutEnb, controlunitv1_1_controlbits[11:0]}

  // Notes on the sheet:
  //   PC-MAR-RAM-IR
endmodule

module computer_t1 (
  input  in_1,
  input  in_2
);

  wire clock_1_out, cpu_4bit_1_ramoutenb, cpu_4bit_1_ramwe;
  wire [3:0] cpu_4bit_1_cmdregout, cpu_4bit_1_insreg, cpu_4bit_1_ramoutput, cpu_4bit_1_rega,
       cpu_4bit_1_regacc, cpu_4bit_1_regout, ram_1_dout;
  wire [7:0] cpu_4bit_1_pc, cpu_4bit_1_ramaddress;

  Clock clock_1 (.out(clock_1_out));
  RAM #(.dataWidth(4)) ram_1 (
    .addr(cpu_4bit_1_ramaddress), .we(cpu_4bit_1_ramwe), .oe(cpu_4bit_1_ramoutenb), .clk(clock_1_out),
    .din(cpu_4bit_1_ramoutput), .dout(ram_1_dout));
  CPU_4bit cpu_4bit_1 (
    .ramInput(ram_1_dout), .CLK(clock_1_out), .clear_CPU(in_2), .regACC(cpu_4bit_1_regacc),
    .PC(cpu_4bit_1_pc), .ramAddress(cpu_4bit_1_ramaddress), .ramWE(cpu_4bit_1_ramwe), .regA(cpu_4bit_1_rega),
    .ramOutEnb(cpu_4bit_1_ramoutenb), .ramOutput(cpu_4bit_1_ramoutput), .insReg(cpu_4bit_1_insreg),
    .regOut(cpu_4bit_1_regout), .cmdRegOUT(cpu_4bit_1_cmdregout));
  Hex_Digit_Display hex_digit_display_1 (.value(cpu_4bit_1_regacc));  // open: dp
  Hex_Digit_Display hex_digit_display_2 (.value(cpu_4bit_1_rega));  // open: dp
  Hex_Digit_Display hex_digit_display_3 (.value(cpu_4bit_1_pc[7:4]));  // open: dp
  Hex_Digit_Display hex_digit_display_4 (.value(cpu_4bit_1_pc[3:0]));  // open: dp
  Hex_Digit_Display hex_digit_display_5 (.value(cpu_4bit_1_regout));  // open: dp
  Hex_Digit_Display hex_digit_display_6 (.value(cpu_4bit_1_insreg));  // open: dp
  Hex_Digit_Display hex_digit_display_7 (.value(cpu_4bit_1_cmdregout));  // open: dp
endmodule
